// Logisim project 2-bit adder.circ as structural Verilog: 1 circuit, main circuit main
module main (
  input  A0,
  input  B0,
  input  A1,
  input  B1
);

  wire and_1_out, and_2_out, and_3_out, or_1_out, xor_1_out, xor_2_out, xor_3_out;

  and and_1 (and_1_out, A0, B0);
  xor xor_1 (xor_1_out, A1, B1);
  and and_2 (and_2_out, A1, B1);
  xor xor_2 (xor_2_out, A0, B0);
  xor xor_3 (xor_3_out, xor_1_out, and_1_out);
  LED S0 (.in(xor_2_out));
  and and_3 (and_3_out, and_1_out, xor_1_out);
  LED carry_bit__overflow (.in(or_1_out));
  or or_1 (or_1_out, and_3_out, and_2_out);
  LED S1 (.in(xor_3_out));
endmodule
