// Logisim project 7-segment display-1.circ as structural Verilog: 1 circuit, main circuit main
module main (
  input  in_1
);

  wire nor_1_out, not_1_out, not_2_out, not_3_out, or_1_out, or_2_out, or_3_out;
  wire [6:0] keyboard_1_data;

  Keyboard keyboard_1 (.clr(in_1), .data(keyboard_1_data));  // open: clk, re, avail
  not not_1 (not_1_out, keyboard_1_data[1]);
  not not_2 (not_2_out, keyboard_1_data[0]);
  or or_1 (or_1_out, not_2_out, keyboard_1_data[1]);
  not not_3 (not_3_out, keyboard_1_data[0]);
  or or_2 (or_2_out, not_1_out, keyboard_1_data[0]);
  or or_3 (or_3_out, keyboard_1_data[0], not_2_out);
  nor nor_1 (nor_1_out, keyboard_1_data[1], keyboard_1_data[0]);
  _7_Segment_Display u_7_segment_display_1 (
    .g(keyboard_1_data[1]), .f(nor_1_out), .a(or_1_out), .b(or_3_out), .e(not_3_out), .d(or_1_out),
    .c(or_2_out));  // open: dp
endmodule
